# Fritzing sketch TicTacToeArduino (saved by Fritzing 0.9.3b)
breadboards: 1

parts:
  LCD1 = LCD screen (I2C)
  Part1 = Arduino Uno (Rev3)
  Part2 = Thumb Joystick

nets:
  GND: LCD1.GND, Part1.GND, Part2.GND
  VCC: LCD1.VCC, Part1.5V, Part2.VCC
  N1: LCD1.SDA, Part1.A4/SDA
  N2: LCD1.SCL, Part1.A5/SCL
  N3: Part1.A0, Part2.HORZ
  N4: Part1.A1, Part2.VERT
  N5: Part1.D7, Part2.SEL

custom parts:
  LCD screen (I2C): A standard character display, usually with 2x16 characters. Comes in many colors.
